// Logisim project 3.circ as structural Verilog: 1 circuit, main circuit main
module main (
);

  wire _4_Counter_carry, and_1_out, and_2_out, CLK, clock_1_out, clock_2_out, d_ff_1_qn, go, J, K, not_1_out,
       or_1_out, Q, Reset_out;
  wire [3:0] _4_Counter_q;

  not not_1 (not_1_out, K);
  and and_1 (and_1_out, J, d_ff_1_qn);
  or or_1 (or_1_out, and_1_out, and_2_out);
  and and_2 (and_2_out, not_1_out, Q);
  Clock clock_1 (.out(clock_1_out));
  D_Flip_Flop d_ff_1 (.clk(clock_1_out), .D(or_1_out), .Q(Q), .Qn(d_ff_1_qn));  // open: preset, en, reset
  TTY #(.rows(1), .cols(16)) tty_1 (.data({6'b011000, Q}), .clk(CLK), .we(go), .clr(Reset_out));
  Button Reset (.out(Reset_out));
  Clock clock_2 (.out(clock_2_out));
  // Probe on _4_Counter_q
  Counter #(.width(4), .max('hf)) _4_Counter (
    .Q(_4_Counter_q), .carry(_4_Counter_carry), .clk(CLK), .clr(Reset_out));  // open: load, D, count
  and and_3 (CLK, clock_2_out, go);
  not not_2 (go, _4_Counter_carry);
  // Probe on J
  ROM #(.addrWidth(4), .dataWidth(2)) rom_1 (.addr(_4_Counter_q), .data({K, J}));  // open: sel
  // Probe on K

  // Notes on the sheet:
  //   001100111101000
  //   contents of rom_1 (hex, n*v repeats v):
  //   0 1 0 2 0 3 0 1 1 2 1 3 2 2 3 3
endmodule
