// Logisim project 4.circ as structural Verilog: 1 circuit, main circuit main
module main (
);

  wire and_1_out, and_2_out, and_3_out, and_5_out, and_6_out, Carry, CLK, clock_1_out, clock_2_out,
       counter_1_carry, D0, D1, D2, D3, Enable, Load, multiplexer_1_out, multiplexer_2_out,
       multiplexer_3_out, multiplexer_4_out, multiplexer_5_out, multiplexer_6_out, multiplexer_7_out,
       multiplexer_8_out, nand_1_out, not_1_out, not_2_out, not_3_out, not_4_out, not_5_out, not_7_out, Q0,
       Q1, Q2, Q3;
  wire [5:1] counter_1_q;

  Clock clock_1 (.out(clock_1_out));
  not not_1 (not_1_out, D0);
  and and_1 (and_1_out, Enable, clock_1_out);
  Multiplexer #(.enable("false")) multiplexer_1 (.in0(D0), .in1(not_1_out), .out(multiplexer_1_out), .sel(Q0));
  Multiplexer #(.enable("false")) multiplexer_2 (
    .in0(1'b1), .in1(multiplexer_1_out), .out(multiplexer_2_out), .sel(Load));
  T_Flip_Flop t_ff_1 (.clk(and_1_out), .T(multiplexer_2_out), .Q(Q0));  // open: Qn, preset, reset, en
  Multiplexer #(.enable("false")) multiplexer_3 (.in0(D1), .in1(not_2_out), .out(multiplexer_3_out), .sel(Q1));
  not not_2 (not_2_out, D1);
  Multiplexer #(.enable("false")) multiplexer_4 (
    .in0(Q0), .in1(multiplexer_3_out), .out(multiplexer_4_out), .sel(Load));
  T_Flip_Flop t_ff_2 (.clk(and_1_out), .T(multiplexer_4_out), .Q(Q1));  // open: Qn, preset, reset, en
  and and_2 (and_2_out, Q1, multiplexer_4_out);
  Multiplexer #(.enable("false")) multiplexer_5 (.in0(D2), .in1(not_3_out), .out(multiplexer_5_out), .sel(Q2));
  not not_3 (not_3_out, D2);
  Multiplexer #(.enable("false")) multiplexer_6 (
    .in0(and_2_out), .in1(multiplexer_5_out), .out(multiplexer_6_out), .sel(Load));
  T_Flip_Flop t_ff_3 (.clk(and_1_out), .T(multiplexer_6_out), .Q(Q2));  // open: Qn, preset, reset, en
  and and_3 (and_3_out, Q2, multiplexer_6_out);
  Multiplexer #(.enable("false")) multiplexer_7 (.in0(D3), .in1(not_4_out), .out(multiplexer_7_out), .sel(Q3));
  not not_4 (not_4_out, D3);
  and and_4 (CLK, clock_2_out, not_5_out);
  Clock clock_2 (.out(clock_2_out));
  Multiplexer #(.enable("false")) multiplexer_8 (
    .in0(and_3_out), .in1(multiplexer_7_out), .out(multiplexer_8_out), .sel(Load));
  TTY #(.rows(1), .cols(37)) tty_1 (.data({2'b10, Carry, Q3, Q2, Q1, Q0}), .clk(CLK));  // open: we, clr
  Counter #(.width(6), .max('h24)) counter_1 (
    .Q({counter_1_q[5], Load, D3, counter_1_q[2:1], D0}), .carry(counter_1_carry), .clk(CLK));  // open: load, D, count, clr
  not not_5 (not_5_out, counter_1_carry);
  T_Flip_Flop t_ff_4 (.clk(and_1_out), .T(multiplexer_8_out), .Q(Q3));  // open: Qn, preset, reset, en
  not not_6 (Enable, counter_1_q[5]);
  and and_5 (and_5_out, Q3, multiplexer_8_out);
  nand nand_1 (nand_1_out, D3, D2, D1, D0);
  or or_1 (D1, Enable, counter_1_q[1]);
  Multiplexer #(.enable("false")) multiplexer_9 (.in0(and_5_out), .in1(not_7_out), .out(Carry), .sel(and_6_out));
  not not_7 (not_7_out, and_5_out);
  and and_6 (and_6_out, nand_1_out, Q3, Q2, Q1, Q0);
  or or_2 (D2, counter_1_q[2], Load);

  // Notes on the sheet:
  //   @ABCDEFGHIJKLMN_@FGFGFGFGN_N_N_N0000
endmodule
