// Logisim project 8-wrong.circ as structural Verilog: 1 circuit, main circuit main
module main (
);

  wire _4_Counter_carry, A_q, A_qn, and_1_out, and_2_out, and_3_out, and_4_out, and_5_out, and_6_out,
       and_7_out, and_8_out, and_9_out, and_10_out, and_11_out, and_12_out, and_13_out, and_14_out,
       and_15_out, and_16_out, and_17_out, and_18_out, and_19_out, B_q, B_qn, C_q, C_qn, CLK, clock_1_out,
       clock_2_out, go, I5, I10, I25, not_1_out, O5, O10, OM, or_1_out, or_2_out, or_3_out, Reset_out,
       undriven, undriven_2;
  wire [4:0] _4_Counter_q;

  not not_1 (not_1_out, I5);
  and and_1 (and_1_out, A_q, B_qn, undriven);
  and and_2 (and_2_out, undriven, A_qn, I5);
  and and_3 (and_3_out, B_qn, I5);
  and and_4 (and_4_out, I25, A_q);
  and and_5 (and_5_out, not_1_out, I10, B_q);
  and and_6 (and_6_out, B_q, not_1_out);
  and and_7 (and_7_out, A_qn, I10, undriven_2);
  and and_8 (and_8_out, undriven_2, B_q, A_q);
  and and_9 (and_9_out, A_q, I5, C_qn, B_qn);
  and and_10 (and_10_out, A_q, C_q);
  and and_11 (and_11_out, A_q, B_q, I5);
  and and_12 (and_12_out, B_q, A_qn, I10);
  and and_13 (and_13_out, B_qn, I10, A_q);
  Clock clock_1 (.out(clock_1_out));
  or or_1 (or_1_out, and_1_out, and_2_out, and_3_out, and_4_out, and_5_out);
  or or_2 (or_2_out, and_6_out, and_7_out, and_8_out, and_9_out);
  or or_3 (or_3_out, and_10_out, and_11_out, and_12_out, and_13_out);
  T_Flip_Flop A (.clk(clock_1_out), .T(or_1_out), .Q(A_q), .Qn(A_qn));  // open: preset, reset, en
  T_Flip_Flop B (.clk(clock_1_out), .T(or_2_out), .Q(B_q), .Qn(B_qn));  // open: preset, reset, en
  T_Flip_Flop C (.clk(clock_1_out), .T(or_3_out), .Q(C_q), .Qn(C_qn));  // open: preset, reset, en
  and and_14 (and_14_out, A_q, B_qn, C_q);
  and and_15 (and_15_out, A_q, B_q, not_1_out);
  or or_4 (OM, and_14_out, I25, and_15_out);
  and and_16 (and_16_out, A_q, I25);
  and and_17 (and_17_out, A_q, C_q, not_1_out);
  and and_18 (and_18_out, B_q, I25);
  and and_19 (and_19_out, A_q, C_q, I25);
  TTY #(.rows(1), .cols(33)) tty_1 (.data({4'b1000, OM, O10, O5}), .clk(CLK), .we(go), .clr(Reset_out));
  Button Reset (.out(Reset_out));
  and and_20 (CLK, clock_2_out, go);
  Clock clock_2 (.out(clock_2_out));
  or or_5 (O5, and_16_out, and_17_out);
  or or_6 (O10, and_18_out, and_19_out);
  // Probe on _4_Counter_q
  Counter #(.width(5), .max('h1f)) _4_Counter (
    .Q(_4_Counter_q), .carry(_4_Counter_carry), .clk(CLK), .clr(Reset_out));  // open: load, D, count
  not not_2 (go, _4_Counter_carry);
  // Probe on I5
  ROM #(.addrWidth(5), .dataWidth(3)) rom_1 (.addr(_4_Counter_q), .data({I25, I10, I5}));  // open: sel
  // Probe on I10
  // Probe on I25

  // Notes on the sheet:
  //   24 Gates
  //   D@@@@D@@@D@@E@E@F@@G@@G@F@@E@@@
  //   contents of rom_1 (hex, n*v repeats v):
  //   4 6*1 2 1 1 2 2 2 1 4 2 4 2 2 4 1 2 4 2 4 2 2 2 1 1 1 2
endmodule
