// Logisim project cpu.circ as structural Verilog: 3 circuits, main circuit register bank
module main (
);

  wire clock_1_out, decoder_1_out0, decoder_1_out1, decoder_1_out2, decoder_1_out3, decoder_1_out4,
       decoder_1_out5, decoder_1_out6;
  wire [9:0] R0, R1, R2, R3, R4, R5, R6;

  LED led_1 (.in(R3[9]));
  LED led_2 (.in(R3[8]));
  LED led_3 (.in(R3[7]));
  LED led_4 (.in(R3[6]));
  LED led_5 (.in(R3[5]));
  LED led_6 (.in(R3[4]));
  LED led_7 (.in(R3[3]));
  LED led_8 (.in(R3[2]));
  LED led_9 (.in(R3[1]));
  LED led_10 (.in(R3[0]));
  Decoder #(.select(3), .enable("false")) decoder_1 (
    .out0(decoder_1_out0), .out1(decoder_1_out1), .out2(decoder_1_out2), .out3(decoder_1_out3),
    .out4(decoder_1_out4), .out5(decoder_1_out5), .out6(decoder_1_out6), .sel(3'b011));  // open: out7
  Clock clock_1 (.out(clock_1_out));
  register_bank register_bank_1 (
    .R0(decoder_1_out0), .R1(decoder_1_out1), .R2(decoder_1_out2), .R3(decoder_1_out3), .R4(decoder_1_out4),
    .R5(decoder_1_out5), .R6(decoder_1_out6), .Clock(clock_1_out), .in_9(1'b1), .in_10(1'b0), .in_11(1'b1),
    .in_12(1'b0), .in_13(1'b1), .in_14(1'b0), .in_15(1'b0), .in_16(1'b0), .in_17(1'b1), .in_18(1'b1),
    .out_19(R0), .out_20(R1), .out_21(R2), .out_22(R3), .out_23(R4), .out_24(R5), .out_25(R6));
endmodule

module register (
  input  Select,
  input  Clock,
  input  in_3,
  input  in_4,
  input  in_5,
  input  in_6,
  input  in_7,
  input  in_8,
  input  in_9,
  input  in_10,
  input  in_11,
  input  in_12,
  output out_13,
  output out_14,
  output out_15,
  output out_16,
  output out_17,
  output out_18,
  output out_19,
  output out_20,
  output out_21,
  output out_22
);

  wire and_1_out;

  and and_1 (and_1_out, Select, Clock);
  D_Flip_Flop d_ff_1 (.clk(and_1_out), .D(in_3), .Q(out_13));  // open: Qn, preset, en, reset
  D_Flip_Flop d_ff_2 (.clk(and_1_out), .D(in_4), .Q(out_14));  // open: Qn, preset, en, reset
  D_Flip_Flop d_ff_3 (.clk(and_1_out), .D(in_5), .Q(out_15));  // open: Qn, preset, en, reset
  D_Flip_Flop d_ff_4 (.clk(and_1_out), .D(in_6), .Q(out_16));  // open: Qn, preset, en, reset
  D_Flip_Flop d_ff_5 (.clk(and_1_out), .D(in_7), .Q(out_17));  // open: Qn, preset, en, reset
  D_Flip_Flop d_ff_6 (.clk(and_1_out), .D(in_8), .Q(out_18));  // open: Qn, preset, en, reset
  D_Flip_Flop d_ff_7 (.clk(and_1_out), .D(in_9), .Q(out_19));  // open: Qn, preset, en, reset
  D_Flip_Flop d_ff_8 (.clk(and_1_out), .D(in_10), .Q(out_20));  // open: Qn, preset, en, reset
  D_Flip_Flop d_ff_9 (.clk(and_1_out), .D(in_11), .Q(out_21));  // open: Qn, preset, en, reset
  D_Flip_Flop d_ff_10 (.clk(and_1_out), .D(in_12), .Q(out_22));  // open: Qn, preset, en, reset
endmodule

module register_bank (
  input  Clock,
  input  R0,
  input  R1,
  input  R2,
  input  R3,
  input  R4,
  input  R5,
  input  R6,
  input  in_9,
  input  in_10,
  input  in_11,
  input  in_12,
  input  in_13,
  input  in_14,
  input  in_15,
  input  in_16,
  input  in_17,
  input  in_18,
  output [9:0] out_19,
  output [9:0] out_20,
  output [9:0] out_21,
  output [9:0] out_22,
  output [9:0] out_23,
  output [9:0] out_24,
  output [9:0] out_25
);

  register register_1 (
    .in_3(in_9), .in_4(in_10), .in_5(in_11), .in_6(in_12), .in_7(in_13), .in_8(in_14), .in_9(in_15),
    .in_10(in_16), .in_11(in_17), .in_12(in_18), .Select(R0), .Clock(Clock), .out_13(out_19[9]),
    .out_14(out_19[8]), .out_15(out_19[7]), .out_16(out_19[6]), .out_17(out_19[5]), .out_18(out_19[4]),
    .out_19(out_19[3]), .out_20(out_19[2]), .out_21(out_19[1]), .out_22(out_19[0]));
  register register_2 (
    .in_3(in_9), .in_4(in_10), .in_5(in_11), .in_6(in_12), .in_7(in_13), .in_8(in_14), .in_9(in_15),
    .in_11(in_17), .in_12(in_18), .Select(R1), .Clock(Clock), .out_13(out_20[9]), .out_14(out_20[8]),
    .out_15(out_20[7]), .out_16(out_20[6]), .out_17(out_20[5]), .out_18(out_20[4]), .out_19(out_20[3]),
    .out_20(out_20[2]), .out_21(out_20[1]), .out_22(out_20[0]));  // open: in_10
  register register_3 (
    .in_3(in_9), .in_4(in_10), .in_5(in_11), .in_6(in_12), .in_7(in_13), .in_8(in_14), .in_9(in_15),
    .in_10(in_16), .in_11(in_17), .in_12(in_18), .Select(R2), .Clock(Clock), .out_13(out_21[9]),
    .out_14(out_21[8]), .out_15(out_21[7]), .out_16(out_21[6]), .out_17(out_21[5]), .out_18(out_21[4]),
    .out_19(out_21[3]), .out_20(out_21[2]), .out_21(out_21[1]), .out_22(out_21[0]));
  register register_4 (
    .in_3(in_9), .in_4(in_10), .in_5(in_11), .in_6(in_12), .in_7(in_13), .in_8(in_14), .in_9(in_15),
    .in_10(in_16), .in_11(in_17), .in_12(in_18), .Select(R3), .Clock(Clock), .out_13(out_22[9]),
    .out_14(out_22[8]), .out_15(out_22[7]), .out_16(out_22[6]), .out_17(out_22[5]), .out_18(out_22[4]),
    .out_19(out_22[3]), .out_20(out_22[2]), .out_21(out_22[1]), .out_22(out_22[0]));
  register register_5 (
    .in_3(in_9), .in_4(in_10), .in_5(in_11), .in_6(in_12), .in_7(in_13), .in_8(in_14), .in_9(in_15),
    .in_10(in_16), .in_11(in_17), .in_12(in_18), .Select(R4), .Clock(Clock), .out_13(out_23[9]),
    .out_14(out_23[8]), .out_15(out_23[7]), .out_16(out_23[6]), .out_17(out_23[5]), .out_18(out_23[4]),
    .out_19(out_23[3]), .out_20(out_23[2]), .out_21(out_23[1]), .out_22(out_23[0]));
  register register_6 (
    .in_3(in_9), .in_4(in_10), .in_5(in_11), .in_6(in_12), .in_7(in_13), .in_8(in_14), .in_9(in_15),
    .in_10(in_16), .in_11(in_17), .in_12(in_18), .Select(R5), .Clock(Clock), .out_13(out_24[9]),
    .out_14(out_24[8]), .out_15(out_24[7]), .out_16(out_24[6]), .out_17(out_24[5]), .out_18(out_24[4]),
    .out_19(out_24[3]), .out_20(out_24[2]), .out_21(out_24[1]), .out_22(out_24[0]));
  register register_7 (
    .in_3(in_9), .in_4(in_10), .in_5(in_11), .in_6(in_12), .in_7(in_13), .in_8(in_14), .in_9(in_15),
    .in_10(in_16), .in_11(in_17), .in_12(in_18), .Select(R6), .Clock(Clock), .out_13(out_25[9]),
    .out_14(out_25[8]), .out_15(out_25[7]), .out_16(out_25[6]), .out_17(out_25[5]), .out_18(out_25[4]),
    .out_19(out_25[3]), .out_20(out_25[2]), .out_21(out_25[1]), .out_22(out_25[0]));
endmodule
